# Fritzing sketch reto_05_a (saved by Fritzing 0.9.3b)
breadboards: 1

parts:
  Componente1 = Arduino Uno (Rev3)
  LED1 = smd LED [color="Green (555nm)" package="0805 [SMD]"]
  LED2 = smd LED [color="Yellow (585nm)" package="0805 [SMD]"]
  LED3 = smd LED [color="Red (633nm)" package="0805 [SMD]"]
  R1 = Resistor [tolerance=±5% resistance=220 package=THT]
  R2 = Resistor [tolerance=±5% resistance=220 package=THT]
  R3 = Resistor [tolerance=±5% resistance=220 package=THT]
  R4 = Resistor [tolerance=±5% resistance=10k package=THT]
  S1 = Momentary Switch [package=ksa_sealed_tac_switch]

nets:
  N1: Componente1.GND, R1.Pin_0, R2.Pin_0, R3.Pin_0, R4.Pin_0
  N2: Componente1.D2, R4.Pin_1, S1.2, S1.4
  N3: Componente1.D3_PWM, LED1.anode
  N4: Componente1.D4, LED2.anode
  N5: Componente1.D5_PWM, LED3.anode
  N6: Componente1.5V, S1.1, S1.3
  N7: LED1.cathode, R1.Pin_1
  N8: LED2.cathode, R2.Pin_1
  N9: LED3.cathode, R3.Pin_1
