# Fritzing sketch reto_08 (saved by Fritzing 0.9.3b)
breadboards: 1

parts:
  Componente1 = Arduino Uno (Rev3)
  R1 = Trimmer Potentiometer [maximum_resistance=10kΩ package=THT]  # not connected
  R2 = Resistor [tolerance=±5% resistance=100 package=THT]
  R3 = Resistor [tolerance=±5% resistance=220 package=THT]
  R4 = Resistor [tolerance=±5% resistance=220 package=THT]
  LED1 = LED - 5mm [color="Red (633nm)" package="5 mm [THT]"]
  LED2 = LED - 5mm [color="Green (555nm)" package="5 mm [THT]"]

nets:
  N1: Componente1.GND, R2.Pin_1, R3.Pin_0, R4.Pin_0
  N2: Componente1.D3_PWM, LED2.anode
  N3: Componente1.D5_PWM, LED1.anode
  N4: R3.Pin_1, LED2.cathode
  N5: R4.Pin_1, LED1.cathode
