# Fritzing sketch reto_09 (saved by Fritzing 0.9.3b)
breadboards: 1

parts:
  Componente1 = Arduino Uno (Rev3)
  LED1 = smd LED [color="Green (555nm)" package="0603 [SMD]"]
  R1 = Resistor [tolerance=±5% resistance=220 package=THT]

nets:
  N1: Componente1.GND, R1.Pin_0
  N2: Componente1.D3_PWM, LED1.anode
  N3: LED1.cathode, R1.Pin_1
