# Fritzing sketch reto_13 (saved by Fritzing 0.9.3b)
breadboards: 1

parts:
  R1 = Trimmer Potentiometer [maximum_resistance=10kΩ package=THT]  # not connected
  R2 = Resistor [tolerance=±5% resistance=100 package=THT]
  Componente1 = Arduino Uno (Rev3)
  J1 = Basic Servo

nets:
  GND: R2.Pin_1, Componente1.GND, J1.gnd
  N1: Componente1.D7, J1.pulse
  5V: Componente1.5V, J1.vcc
