# Fritzing sketch reto_17 (saved by Fritzing 0.9.3b)
breadboards: 1

parts:
  Componente1 = Arduino Uno (Rev3)
  S1 = Pushbutton [package="[THT]"]
  Componente2 = Arduino Uno (Rev3)
  R2 = Resistor [tolerance=±5% resistance=10k package=THT]

nets:
  GND: Componente1.GND, Componente2.GND, R2.Pin_0
  N1: Componente1.D0/RX, Componente2.D1/TX
  N2: Componente1.D1/TX, Componente2.D0/RX
  N3: Componente1.D2, Componente1.5V, S1.Pin_1, S1.Pin_2, S1.Pin_3, S1.Pin_4, R2.Pin_1
