# Fritzing sketch reto_0_a (saved by Fritzing 0.9.0b)
breadboards: 1

parts:
  R1 = Resistor [tolerance=±5% resistance=220 package=THT]
  LED1 = LED - 5mm [color="Red (633nm)" package="5 mm [THT]"]
  V1 = DC Power [voltage=5]  # not connected
  Parte1 = Arduino Uno (Rev3)

nets:
  N1: R1.Pin_0, Parte1.5V
  N2: R1.Pin_1, LED1.cathode
  N3: LED1.anode, Parte1.GND
