# Fritzing sketch reto_0_b (saved by Fritzing 0.9.0b)
breadboards: 1

parts:
  LED1 = LED - 5mm [color="Red (633nm)" package="5 mm [THT]"]
  R1 = Resistor [tolerance=±5% resistance=220 package=THT]
  VCC1 = Battery

nets:
  N1: LED1.cathode, VCC1.-
  N2: LED1.anode, R1.Pin_0
  N3: R1.Pin_1, VCC1.+
