# Fritzing sketch reto_07 (saved by Fritzing 0.9.3b)
breadboards: 1

parts:
  R1 = Resistor [tolerance=±5% resistance=470 package=THT]
  Componente1 = Arduino Uno (Rev3)
  R2 = Photocell (LDR) [package=THT]
  LED1 = LED - 5mm [color="Green (555nm)" package="5 mm [THT]"]
  R3 = Resistor [tolerance=±5% resistance=220 package=THT]

nets:
  N1: R1.Pin_0, Componente1.5V
  N2: R1.Pin_1, Componente1.A1, R2.pin_0
  N3: Componente1.GND, R2.pin_1, R3.Pin_0
  N4: Componente1.D3_PWM, LED1.anode
  N5: LED1.cathode, R3.Pin_1
