# Fritzing sketch reto_10 (saved by Fritzing 0.9.3b)
breadboards: 1

parts:
  Componente1 = Arduino Uno (Rev3)
  LED1 = smd LED [color="Green (555nm)" package="0603 [SMD]"]
  R1 = Resistor [tolerance=±5% resistance=220 package=THT]
  R2 = Resistor [tolerance=±5% resistance=10k package=THT]
  S1 = Square Pushbutton

nets:
  N1: Componente1.GND, R1.Pin_0, R2.Pin_1
  N2: Componente1.D2, R2.Pin_0, S1.leg0
  N3: Componente1.D3_PWM, LED1.anode
  N4: Componente1.5V, S1.leg1
  N5: LED1.cathode, R1.Pin_1
