# Fritzing sketch reto_14 (saved by Fritzing 0.9.3b)
breadboards: 1

parts:
  Componente1 = Arduino Uno (Rev3)
  J1 = Basic Servo

nets:
  GND: Componente1.GND, J1.gnd
  N1: Componente1.D7, J1.pulse
  5V: Componente1.5V, J1.vcc
