# Fritzing sketch reto_15 (saved by Fritzing 0.9.3b)
breadboards: 1

parts:
  Componente1 = Arduino Uno (Rev3)
  R1 = Resistor [tolerance=±5% resistance=220 package=THT]
  LED1 = LED - 3mm [color="Green (555nm)" package="3 mm [THT]"]

nets:
  N1: Componente1.GND, R1.Pin_0
  N2: Componente1.D3_PWM, LED1.anode
  N3: R1.Pin_1, LED1.cathode
