# Fritzing sketch reto_16 (saved by Fritzing 0.9.3b)
breadboards: 1

parts:
  Componente1 = Arduino Uno (Rev3)
  R1 = Resistor [tolerance=±5% resistance=220 package=THT]
  LED1 = LED - 3mm [color="Green (555nm)" package="3 mm [THT]"]
  R2 = Resistor [tolerance=±5% resistance=10k package=THT]
  R3 = Photocell (LDR) [package=THT]

nets:
  N1: Componente1.A1, R2.Pin_1, R3.pin_1
  N2: Componente1.GND, R1.Pin_0, R2.Pin_0
  N3: Componente1.D3_PWM, LED1.anode
  N4: Componente1.5V, R3.pin_0
  N5: R1.Pin_1, LED1.cathode
