# Fritzing sketch barrera_servo_ldr (saved by Fritzing 0.9.3b)
breadboards: 1

parts:
  Arduino_Uno = Arduino Uno (Rev3)
  LDR = Photocell (LDR) [package=THT]
  Resistencia = Resistor [tolerance=±5% resistance=10k package=THT]
  Servo = Basic Servo
  Led_rojo = smd LED [color="Red (633nm)" package="1206 [SMD]"]
  Led_verde = smd LED [color="Green (565nm)" package="1206 [SMD]"]
  R1 = Resistor [tolerance=±5% resistance=220 package=THT]
  R2 = Resistor [tolerance=±5% resistance=220 package=THT]

nets:
  N1: Arduino_Uno.A0, LDR.pin_0, Resistencia.Pin_1
  N2: Arduino_Uno.D9_PWM, Servo.pulse
  N3: Arduino_Uno.D12/MISO, Led_verde.anode
  N4: Arduino_Uno.D13/SCK, Led_rojo.anode
  5V: Arduino_Uno.5V, LDR.pin_1, Servo.vcc
  GND: Arduino_Uno.GND, Resistencia.Pin_0, Servo.gnd, R1.Pin_0, R2.Pin_0
  N5: Led_rojo.cathode, R1.Pin_1
  N6: Led_verde.cathode, R2.Pin_1
